# Fritzing sketch breadboard_lamp_layout_5V (saved by Fritzing 0.7.4b)
breadboards: 1

parts:
  LED1 = Sparkfun Piranha RGB LED COM-10390 (com. cathode) [part_number=1P05S3UGB01DA301]
  R1 = Resistor [tolerance=±5% resistance=130 package=THT]
  R2 = Resistor [tolerance=±5% resistance=75 package="1206 [SMD]"]
  R2_2 = Resistor [tolerance=±5% resistance=75 package=THT]
  Nano1 = Arduino Nano v2.3
  LED2 = Sparkfun Piranha RGB LED COM-10390 (com. cathode) [part_number=1P05S3UGB01DA301]
  R9 = Resistor [tolerance=±5% resistance=130 package=THT]
  R10 = Resistor [tolerance=±5% resistance=75 package=THT]
  R11 = Resistor [tolerance=±5% resistance=75 package=THT]
  U1 = mystery part, 4 pins [chip_label="RX 433" spacing=300mil part_number=CDR03A]

nets:
  N1: LED1.red_anode, R1.Pin_0
  N2: LED1.green_anode, R2.Pin_0
  N3: LED1.blue_anode, R2_2.Pin_0
  N4: LED1.common_cathode, Nano1.GND, LED2.common_cathode, U1.pin1
  N5: R1.Pin_1, Nano1.D3
  N6: R2.Pin_1, Nano1.D5
  N7: R2_2.Pin_1, Nano1.D6
  N8: Nano1.D7, U1.pin2
  N9: Nano1.D9, R9.Pin_1
  N10: Nano1.D10, R10.Pin_1
  N11: Nano1.D11, R11.Pin_1
  N12: Nano1.+5V, U1.pin4
  N13: LED2.red_anode, R9.Pin_0
  N14: LED2.green_anode, R10.Pin_0
  N15: LED2.blue_anode, R11.Pin_0

custom parts:
  Sparkfun Piranha RGB LED COM-10390 (com. cathode): Sparkfun's Piranha 5mm RGB LEDs for breadboard mount. These RGB LEDs fit nicely into PCBs or breadboards because of their square shape. They are common cathode and pretty bright for their size. DC forward current: 20mA Forward voltage: red: 1.8 - 2.5V green: 3.0 - 3.5V blue: 3.0 - 3.5V
