# Fritzing sketch breadboard_sender_layout_5V (saved by Fritzing 0.7.4b)
breadboards: 1

parts:
  Arduino1 = Arduino
  U1 = mystery part, 4 pins [chip_label="TX 433" spacing=300mil]

nets:
  N1: Arduino1.D12, U1.pin2
  N2: Arduino1.+5V, U1.pin4
  N3: Arduino1.GND, U1.pin3
